# Fritzing sketch servo (saved by Fritzing 0.9.2b)
breadboards: 1

parts:
  Part3 = Arduino Uno (Rev3)
  J1 = Basic Servo
  VCC1 = Battery

nets:
  N1: Part3.D10_PWM/SS, J1.pulse
  GND: Part3.GND, J1.gnd, VCC1.-
  N2: J1.vcc, VCC1.+
